# Fritzing sketch Esquematico (saved by Fritzing 1.0.7)
breadboards: 1

parts:
  R1 = Resistor [tolerance=±5% power=0.25W resistance=220 package=THT]
  Componente1 = Arduino Uno (Rev3) - ICSP
  LED1 = smd LED [color="Red (633nm)" package="1206 [SMD]"]

nets:
  N1: R1.Pin_0, Componente1.GND
  N2: R1.Pin_1, LED1.cathode
  N3: Componente1.D13/SCK, LED1.anode
